# Fritzing sketch keyclickCircuit (saved by Fritzing 0.9.2b)
circuit board: 8.56404cm x 4.46513cm
breadboards: 1

parts:
  J1 = Power Jack [package=power_jack_pth_lock]
  U1 = Voltage Regulator - 5V [package="TO220 [THT]"]
  C1 = Electrolytic Capacitor [capacitance=1µF package="100 mil [THT, electrolytic]"]
  C2 = Electrolytic Capacitor [capacitance=1µF package="100 mil [THT, electrolytic]"]
  J2 = COMPUTER-PERIPHERAL-POWER [package=computer-peripheral-power]
  Q1 = npn-Powertransistor [package="TO220 [THT]"]
  D1 = Diode [package=diode-1n4001]
  Q2 = NPN-Transistor [package="TO92 [THT]"]
  R1 = Resistor [tolerance=±5% resistance=220 package=THT]
  R2 = Resistor [tolerance=±5% resistance=220 package=THT]
  LED1 = LED - 5mm [color="Red (633nm)" package="5 mm [THT]"]
  R3 = Resistor [tolerance=±5% resistance=220 package=THT]
  JP1 = Header 12 [package=1x12_machine-pin-header_lock.004]
  JP2 = Header 12 [package=1x12_machine-pin-header_lock.004]

nets:
  GND: J1.GND, J1.GNDBREAK, U1.GND, C1.-, C2.-, Q1.emitter, D1.A, LED1.cathode, JP1.1
  N1: J1.PWR, U1.input_voltage, C2.+, J2.5V, D1.C
  N2: U1.output_voltage, C1.+, Q2.C, JP1.2
  N3: J2.GND, Q1.collector
  N4: Q1.base, R2.Pin_0
  N5: Q2.E, R3.Pin_1
  N6: Q2.B, R1.Pin_0
  N7: R1.Pin_1, R2.Pin_1, JP1.3
  N8: LED1.anode, R3.Pin_0
  N9: JP2.10, JP2.11
